// Logisim project TASK3 USING NAND.circ as structural Verilog: 4 circuits, main circuit main
module main (
  input  A,
  input  B,
  input  C,
  output out_4
);

  wire and_ic_1_out_5, and_ic_1_out_6, not_ic_1_out_3;

  NOT_IC not_ic_1 (.in_1(C), .out_3(not_ic_1_out_3));  // open: in_2, out_4
  AND_IC and_ic_1 (.in_1(C), .in_2(A), .in_3(B), .in_4(not_ic_1_out_3), .out_5(and_ic_1_out_5), .out_6(and_ic_1_out_6));
  OR_IC or_ic_1 (.in_1(and_ic_1_out_5), .in_2(and_ic_1_out_6), .out_5(out_4));  // open: in_3, in_4, out_6
endmodule

// A N D
module AND_IC (
  input  in_1,
  input  in_2,
  input  in_3,
  input  in_4,
  output out_5,
  output out_6
);

  wire nand_1_out, nand_2_out;

  nand nand_1 (nand_1_out, in_1, in_2);
  nand nand_2 (nand_2_out, in_3, in_4);
  nand nand_3 (out_5, nand_1_out, nand_1_out);
  nand nand_4 (out_6, nand_2_out, nand_2_out);
endmodule

// O R
module OR_IC (
  input  in_1,
  input  in_2,
  input  in_3,
  input  in_4,
  output out_5,
  output out_6
);

  wire nand_1_out, nand_2_out, nand_3_out, nand_4_out;

  nand nand_1 (nand_1_out, in_1, in_1);
  nand nand_2 (nand_2_out, in_2, in_2);
  nand nand_3 (nand_3_out, in_3, in_3);
  nand nand_4 (nand_4_out, in_4, in_4);
  nand nand_5 (out_5, nand_1_out, nand_2_out);
  nand nand_6 (out_6, nand_3_out, nand_4_out);
endmodule

// N O T
module NOT_IC (
  input  in_1,
  input  in_2,
  output out_3,
  output out_4
);

  nand nand_1 (out_3, in_1, in_1);
  nand nand_2 (out_4, in_2, in_2);
endmodule
