// Logisim project TASK3 USING NOR.circ as structural Verilog: 4 circuits, main circuit main
module main (
  input  A,
  input  B,
  input  C,
  output out_4
);

  wire and_ic_1_out_5, and_ic_1_out_6, not_ic_1_out_2;

  NOT_IC not_ic_1 (.in_1(C), .out_2(not_ic_1_out_2));
  AND_IC and_ic_1 (.in_1(C), .in_2(A), .out_5(and_ic_1_out_5), .in_3(B), .out_6(and_ic_1_out_6), .in_4(not_ic_1_out_2));
  OR_IC or_ic_1 (.in_1(and_ic_1_out_5), .in_2(and_ic_1_out_6), .out_3(out_4));
endmodule

// AND
module AND_IC (
  input  in_1,
  input  in_2,
  input  in_3,
  input  in_4,
  output out_5,
  output out_6
);

  wire nor_1_out, nor_2_out, nor_3_out, nor_4_out;

  nor nor_1 (nor_1_out, in_1, in_1);
  nor nor_2 (nor_2_out, in_2, in_2);
  nor nor_3 (nor_3_out, in_3, in_3);
  nor nor_4 (nor_4_out, in_4, in_4);
  nor nor_5 (out_5, nor_1_out, nor_2_out);
  nor nor_6 (out_6, nor_3_out, nor_4_out);
endmodule

// OR
module OR_IC (
  input  in_1,
  input  in_2,
  output out_3
);

  wire nor_1_out;

  nor nor_1 (nor_1_out, in_1, in_2);
  nor nor_2 (out_3, nor_1_out, nor_1_out);
endmodule

// NOT
module NOT_IC (
  input  in_1,
  output out_2
);

  nor nor_1 (out_2, in_1, in_1);
endmodule
